# Fritzing sketch LED_1 (saved by Fritzing 0.9.5d)
circuit board: 7.54923cm x 2.50664cm
breadboards: 1

parts:
  Raspberry_Pi_Pico = Raspberry Pi Pico W
  LED2 = LED - 5mm [color="Red (633nm)" package="5 mm [THT]"]
  R3 = Resistor [tolerance=±5% resistance=220 package=THT]
  LED3 = LED - 5mm [color="Green (565nm)" package="5 mm [THT]"]
  R4 = Resistor [tolerance=±5% resistance=220 package=THT]

nets:
  N1: Raspberry_Pi_Pico.pin_3, Raspberry_Pi_Pico.pin_8, Raspberry_Pi_Pico.pin_13, Raspberry_Pi_Pico.pin_18, Raspberry_Pi_Pico.pin_23, Raspberry_Pi_Pico.pin_28, Raspberry_Pi_Pico.pin_33, Raspberry_Pi_Pico.pin_38, LED2.cathode, LED3.cathode
  N2: Raspberry_Pi_Pico.pin_20, R4.Pin_1
  N3: Raspberry_Pi_Pico.pin_36, R3.Pin_1
  N4: LED2.anode, R3.Pin_0
  N5: LED3.anode, R4.Pin_0

custom parts:
  Raspberry Pi Pico W: Raspberry Pi Pico W. Based around the RP2040 microcontroller the Pico W is a low cost microcontroller device bringing Raspberry Pi quality, cost, and easy of use to the microcontroller space. The areas marked KEEPOUT in pcb silkscreen should not have traces running through them to avoid shorts on a soldered in module!
