# Fritzing sketch Pot_1 (saved by Fritzing 0.9.5d)
breadboards: 1

parts:
  Mod1 = Raspberry Pi Pico W
  R2 = Rotary Potentiometer (Small) [maximum_resistance=10kΩ package=THT]
  R1 = Resistor [tolerance=±5% resistance=220 package="0402 [SMD]"]
  LED1 = LED - 5mm [color="Red (633nm)" package="5 mm [THT]"]
  R3 = Resistor [tolerance=±5% resistance=220 package="0402 [SMD]"]
  LED2 = LED - 5mm [color="Green (560nm)" package="5 mm [THT]"]

nets:
  N1: Mod1.pin_3, Mod1.pin_8, Mod1.pin_13, Mod1.pin_18, Mod1.pin_23, Mod1.pin_28, Mod1.pin_33, Mod1.pin_38, R2.leg1, R1.Pin_1
  N2: Mod1.pin_36, R2.leg2, R3.Pin_1
  N3: R2.wiper, LED1.anode, LED2.cathode
  N4: R1.Pin_0, LED1.cathode
  N5: R3.Pin_0, LED2.anode

custom parts:
  Raspberry Pi Pico W: Raspberry Pi Pico W. Based around the RP2040 microcontroller the Pico W is a low cost microcontroller device bringing Raspberry Pi quality, cost, and easy of use to the microcontroller space. The areas marked KEEPOUT in pcb silkscreen should not have traces running through them to avoid shorts on a soldered in module!
