# Fritzing sketch HC-SR501 (saved by Fritzing 0.9.5d)
breadboards: 1

parts:
  Mod1 = Raspberry Pi Pico W
  A1 = HC-SR501 Body Sensor Module

nets:
  N1: Mod1.pin_3, Mod1.pin_8, Mod1.pin_13, Mod1.pin_18, Mod1.pin_23, Mod1.pin_28, Mod1.pin_33, Mod1.pin_38, A1.GND
  N2: Mod1.pin_12, A1.OUT
  N3: Mod1.pin_40, A1.VCC

custom parts:
  Raspberry Pi Pico W: Raspberry Pi Pico W. Based around the RP2040 microcontroller the Pico W is a low cost microcontroller device bringing Raspberry Pi quality, cost, and easy of use to the microcontroller space. The areas marked KEEPOUT in pcb silkscreen should not have traces running through them to avoid shorts on a soldered in module!
  HC-SR501 Body Sensor Module: Pyroelectric Infrared PIR Motion Sensor Detector Module
